// Logisim project cpu.circ as structural Verilog: 5 circuits, main circuit main
module main (
);

  wire [7:0] register_1_q;

  Register register_1 (.Q(register_1_q));  // open: D, en, clk, clr
  RAM #(.dataWidth(16)) ram_1 (.addr(register_1_q));  // open: data, sel, clk, ld, clr
  alu_16bit alu_16bit_1 ();  // open: a, b, result, a_inv, b_inv, carry_in, op, zero, c_out, overflow
  RAM #(.dataWidth(16)) ram_2 ();  // open: addr, data, sel, clk, ld, clr
endmodule

module register_file (
  input  [1:0] read_register1,
  input  [15:0] write_data,
  input  write_signal,
  input  [1:0] write_register,
  input  [1:0] read_register2,
  input  clock,
  output [15:0] read_data1,
  output [15:0] read_data2
);

  wire and_1_out, and_2_out, and_3_out, and_4_out, decoder_1_out0, decoder_1_out1, decoder_1_out2,
       decoder_1_out3;
  wire [15:0] register_1_q, register_2_q, register_3_q, register_4_q;

  Decoder #(.select(2)) decoder_1 (
    .out0(decoder_1_out0), .out1(decoder_1_out1), .out2(decoder_1_out2), .out3(decoder_1_out3),
    .sel(write_register));  // open: en
  and and_1 (and_1_out, write_signal, decoder_1_out0);
  and and_2 (and_2_out, write_signal, decoder_1_out1);
  and and_3 (and_3_out, write_signal, decoder_1_out2);
  and and_4 (and_4_out, decoder_1_out3, write_signal);
  Register #(.width(16)) register_1 (.D(write_data), .en(and_1_out), .Q(register_1_q), .clk(clock));  // open: clr
  Register #(.width(16)) register_2 (.D(write_data), .en(and_2_out), .Q(register_2_q), .clk(clock));  // open: clr
  Register #(.width(16)) register_3 (.D(write_data), .en(and_3_out), .Q(register_3_q), .clk(clock));  // open: clr
  Register #(.width(16)) register_4 (.D(write_data), .en(and_4_out), .Q(register_4_q), .clk(clock));  // open: clr
  Multiplexer #(.select(2), .width(16)) multiplexer_1 (
    .in0(register_1_q), .in1(register_2_q), .in2(register_3_q), .in3(register_4_q), .out(read_data1),
    .sel(read_register1));  // open: en
  Multiplexer #(.select(2), .width(16)) multiplexer_2 (
    .in0(register_1_q), .in1(register_2_q), .in2(register_3_q), .in3(register_4_q), .out(read_data2),
    .sel(read_register2));  // open: en
endmodule

module alu_1bit (
  input  carry_in,
  input  in_2,
  input  a_invert,
  input  in_4,
  input  [1:0] opp,
  input  b_invert,
  input  less,
  output result,
  output carry_out
);

  wire adder_1_out, and_1_out, multiplexer_1_out, multiplexer_2_out, not_1_out, not_2_out, or_1_out;

  not not_1 (not_1_out, in_2);
  not not_2 (not_2_out, in_4);
  Multiplexer multiplexer_1 (.in0(in_4), .in1(not_2_out), .out(multiplexer_1_out), .sel(b_invert));  // open: en
  Multiplexer multiplexer_2 (.in0(in_2), .in1(not_1_out), .out(multiplexer_2_out), .sel(a_invert));  // open: en
  and and_1 (and_1_out, multiplexer_2_out, multiplexer_1_out);
  or or_1 (or_1_out, multiplexer_2_out, multiplexer_1_out);
  Adder #(.width(1)) adder_1 (
    .a(multiplexer_2_out), .b(multiplexer_1_out), .out(adder_1_out), .cin(carry_in), .cout(carry_out));
  Multiplexer #(.select(2)) multiplexer_3 (
    .in0(and_1_out), .in1(or_1_out), .in2(adder_1_out), .in3(less), .out(result), .sel(opp));  // open: en
endmodule

module alu_1bit_last (
  input  carry_in,
  input  in_2,
  input  a_invert,
  input  in_4,
  input  [1:0] opp,
  input  b_invert,
  input  less,
  output result,
  output set,
  output carry_out,
  output overflow
);

  wire and_1_out, multiplexer_1_out, multiplexer_2_out, not_1_out, not_2_out, or_1_out;

  not not_1 (not_1_out, in_2);
  not not_2 (not_2_out, in_4);
  Multiplexer multiplexer_1 (.in0(in_4), .in1(not_2_out), .out(multiplexer_1_out), .sel(b_invert));  // open: en
  Multiplexer multiplexer_2 (.in0(in_2), .in1(not_1_out), .out(multiplexer_2_out), .sel(a_invert));  // open: en
  and and_1 (and_1_out, multiplexer_2_out, multiplexer_1_out);
  or or_1 (or_1_out, multiplexer_2_out, multiplexer_1_out);
  Adder #(.width(1)) adder_1 (
    .a(multiplexer_2_out), .b(multiplexer_1_out), .out(set), .cin(carry_in), .cout(carry_out));
  xor xor_1 (overflow, carry_out, carry_in);
  Multiplexer #(.select(2)) multiplexer_3 (
    .in0(and_1_out), .in1(or_1_out), .in2(set), .in3(less), .out(result), .sel(opp));  // open: en
endmodule

module alu_16bit (
  input  [15:0] a,
  input  carry_in,
  input  b_inv,
  input  a_inv,
  input  [1:0] op,
  input  [15:0] b,
  output [15:0] result,
  output zero,
  output c_out,
  output overflow
);

  wire alu_1bit_1_carry_out, alu_1bit_2_carry_out, alu_1bit_3_carry_out, alu_1bit_4_carry_out,
       alu_1bit_5_carry_out, alu_1bit_6_carry_out, alu_1bit_7_carry_out, alu_1bit_8_carry_out,
       alu_1bit_9_carry_out, alu_1bit_10_carry_out, alu_1bit_11_carry_out, alu_1bit_12_carry_out,
       alu_1bit_13_carry_out, alu_1bit_14_carry_out, alu_1bit_15_carry_out, alu_1bit_last_1_set;

  alu_1bit alu_1bit_1 (
    .carry_in(carry_in), .in_2(a[0]), .a_invert(a_inv), .in_4(b[0]), .opp(op), .b_invert(b_inv),
    .less(alu_1bit_last_1_set), .result(result[0]), .carry_out(alu_1bit_1_carry_out));
  alu_1bit alu_1bit_2 (
    .carry_in(alu_1bit_1_carry_out), .in_2(a[1]), .a_invert(a_inv), .in_4(b[1]), .opp(op), .b_invert(b_inv),
    .less(1'b0), .result(result[1]), .carry_out(alu_1bit_2_carry_out));
  alu_1bit alu_1bit_3 (
    .carry_in(alu_1bit_2_carry_out), .in_2(a[2]), .a_invert(a_inv), .in_4(b[2]), .opp(op), .b_invert(b_inv),
    .less(1'b0), .result(result[2]), .carry_out(alu_1bit_3_carry_out));
  alu_1bit alu_1bit_4 (
    .carry_in(alu_1bit_3_carry_out), .in_2(a[3]), .a_invert(a_inv), .in_4(b[3]), .opp(op), .b_invert(b_inv),
    .less(1'b0), .result(result[3]), .carry_out(alu_1bit_4_carry_out));
  alu_1bit alu_1bit_5 (
    .carry_in(alu_1bit_4_carry_out), .in_2(a[4]), .a_invert(a_inv), .in_4(b[4]), .opp(op), .b_invert(b_inv),
    .less(1'b0), .result(result[4]), .carry_out(alu_1bit_5_carry_out));
  alu_1bit alu_1bit_6 (
    .carry_in(alu_1bit_5_carry_out), .in_2(a[5]), .a_invert(a_inv), .in_4(b[5]), .opp(op), .b_invert(b_inv),
    .less(1'b0), .result(result[5]), .carry_out(alu_1bit_6_carry_out));
  alu_1bit alu_1bit_7 (
    .carry_in(alu_1bit_6_carry_out), .in_2(a[6]), .a_invert(a_inv), .in_4(b[6]), .opp(op), .b_invert(b_inv),
    .less(1'b0), .result(result[6]), .carry_out(alu_1bit_7_carry_out));
  alu_1bit alu_1bit_8 (
    .carry_in(alu_1bit_7_carry_out), .in_2(a[7]), .a_invert(a_inv), .in_4(b[7]), .opp(op), .b_invert(b_inv),
    .less(1'b0), .result(result[7]), .carry_out(alu_1bit_8_carry_out));
  alu_1bit alu_1bit_9 (
    .carry_in(alu_1bit_8_carry_out), .in_2(a[8]), .a_invert(a_inv), .in_4(b[8]), .opp(op), .b_invert(b_inv),
    .less(1'b0), .result(result[8]), .carry_out(alu_1bit_9_carry_out));
  alu_1bit alu_1bit_10 (
    .carry_in(alu_1bit_9_carry_out), .in_2(a[9]), .a_invert(a_inv), .in_4(b[9]), .opp(op), .b_invert(b_inv),
    .less(1'b0), .result(result[9]), .carry_out(alu_1bit_10_carry_out));
  alu_1bit alu_1bit_11 (
    .carry_in(alu_1bit_10_carry_out), .in_2(a[10]), .a_invert(a_inv), .in_4(b[10]), .opp(op),
    .b_invert(b_inv), .less(1'b0), .result(result[11]), .carry_out(alu_1bit_11_carry_out));
  alu_1bit alu_1bit_12 (
    .carry_in(alu_1bit_11_carry_out), .in_2(a[11]), .a_invert(a_inv), .in_4(b[11]), .opp(op),
    .b_invert(b_inv), .less(1'b0), .result(result[10]), .carry_out(alu_1bit_12_carry_out));
  alu_1bit alu_1bit_13 (
    .carry_in(alu_1bit_12_carry_out), .in_2(a[12]), .a_invert(a_inv), .in_4(b[12]), .opp(op),
    .b_invert(b_inv), .less(1'b0), .result(result[12]), .carry_out(alu_1bit_13_carry_out));
  alu_1bit alu_1bit_14 (
    .carry_in(alu_1bit_13_carry_out), .in_2(a[13]), .a_invert(a_inv), .in_4(b[13]), .opp(op),
    .b_invert(b_inv), .less(1'b0), .result(result[13]), .carry_out(alu_1bit_14_carry_out));
  alu_1bit alu_1bit_15 (
    .carry_in(alu_1bit_14_carry_out), .in_2(a[14]), .a_invert(a_inv), .in_4(b[14]), .opp(op),
    .b_invert(b_inv), .less(1'b0), .result(result[14]), .carry_out(alu_1bit_15_carry_out));
  alu_1bit_last alu_1bit_last_1 (
    .carry_in(alu_1bit_15_carry_out), .in_2(a[15]), .a_invert(a_inv), .in_4(b[15]), .opp(op),
    .b_invert(b_inv), .less(1'b0), .result(result[15]), .set(alu_1bit_last_1_set), .carry_out(c_out),
    .overflow(overflow));
  nor nor_1 (zero, result[0], result[1], result[2], result[3], result[4], result[5], result[6], result[7], result[8], result[9], result[10], result[11], result[12], result[13], result[14], result[15]);
endmodule
